# Fritzing sketch shake sensor circuit (saved by Fritzing 0.9.3b)
circuit board: 8.46667cm x 5.64444cm
perfboards: 1

parts:
  LED2 = smd LED [color="Blue (470nm)" package="0603 [SMD]"]
  R1 = Resistor [tolerance=±5% resistance=330 package="2512 [SMD]"]
  R2 = Resistor [tolerance=±5% resistance=330 package="2512 [SMD]"]
  XYZ_Sensor = Triple Axis Accelerometer Breakout - ADXL335
  LED1 = smd LED [color="Green (560nm)" package="0603 [SMD]"]
  R3 = Resistor [tolerance=±5% resistance=330 package="2512 [SMD]"]
  LED3 = smd LED [color="Red (633nm)" package="0603 [SMD]"]
  adriono_nano = Arduino Nano (Rev3.0)
  LED4 = smd LED [color="Red (633nm)" package="0603 [SMD]"]
  R4 = Resistor [tolerance=±5% resistance=330 package="2512 [SMD]"]
  LED5 = smd LED [color="Red (633nm)" package="0603 [SMD]"]
  LED6 = smd LED [color="Red (633nm)" package="0603 [SMD]"]
  LED7 = smd LED [color="Red (633nm)" package="0603 [SMD]"]
  LED8 = smd LED [color="Red (633nm)" package="0603 [SMD]"]
  LED9 = smd LED [color="Red (633nm)" package="0603 [SMD]"]
  LED10 = smd LED [color="Red (633nm)" package="0603 [SMD]"]
  LED11 = smd LED [color="Red (633nm)" package="0603 [SMD]"]
  LED12 = smd LED [color="Blue (525nm)" package="0603 [SMD]"]
  LED13 = smd LED [color="Red (633nm)" package="0603 [SMD]"]
  LED14 = smd LED [color="Red (633nm)" package="0603 [SMD]"]
  LED15 = smd LED [color="Red (633nm)" package="0603 [SMD]"]
  LED16 = smd LED [color="Red (633nm)" package="0603 [SMD]"]
  LED17 = smd LED [color="Red (633nm)" package="0603 [SMD]"]
  LED18 = smd LED [color="Red (633nm)" package="0603 [SMD]"]
  LED19 = smd LED [color="Red (633nm)" package="0603 [SMD]"]
  LED20 = smd LED [color="Red (633nm)" package="0603 [SMD]"]
  LED21 = smd LED [color="Red (633nm)" package="0603 [SMD]"]
  LED22 = smd LED [color="Red (633nm)" package="0603 [SMD]"]
  LED23 = smd LED [color="Red (633nm)" package="0603 [SMD]"]
  LED24 = smd LED [color="Red (633nm)" package="0603 [SMD]"]
  R5 = Resistor [tolerance=±5% resistance=330 package="2512 [SMD]"]
  R6 = Resistor [tolerance=±5% resistance=330 package="2512 [SMD]"]

nets (from the schematic view):
  N1: LED2.cathode, R1.Pin_1
  N2: LED2.anode, LED1.anode, LED3.anode, adriono_nano.GND, LED4.anode, LED9.anode, LED10.anode, LED12.anode, LED13.anode, LED14.anode, LED19.anode, LED20.anode, LED21.anode
  N3: R1.Pin_0, adriono_nano.D12/MISO, R4.Pin_0
  N4: R2.Pin_0, adriono_nano.D11/MOSI, R5.Pin_0
  N5: R2.Pin_1, LED1.cathode
  N6: XYZ_Sensor.ZOUT, adriono_nano.A0
  N7: XYZ_Sensor.YOUT, adriono_nano.A1
  N8: XYZ_Sensor.XOUT, adriono_nano.A2
  N9: XYZ_Sensor.GND, adriono_nano.A3
  N10: XYZ_Sensor.VCC, adriono_nano.A4
  N11: R3.Pin_0, adriono_nano.D10, R6.Pin_0
  N12: R3.Pin_1, LED3.cathode
  N13: LED4.cathode, LED6.cathode
  N14: R4.Pin_1, LED5.cathode, LED7.cathode, LED8.cathode, LED9.cathode, LED10.cathode
  N15: LED5.anode, LED8.anode
  N16: LED6.anode, LED7.anode
  N17: LED11.cathode, LED12.cathode, LED13.cathode, LED14.cathode, LED15.cathode, LED16.cathode, LED17.cathode, R5.Pin_1
  N18: LED11.anode, LED15.anode
  N19: LED16.anode, LED17.anode
  N20: LED18.cathode, LED19.cathode, LED20.cathode, LED21.cathode, LED22.cathode, LED23.cathode, LED24.cathode, R6.Pin_1
  N21: LED18.anode, LED22.anode
  N22: LED23.anode, LED24.anode

// code stored in the sketch: shakesenser.ino

const int groundpin = 18; // analog input pin 4 -- ground


const int powerpin = 19; // analog input pin 5 -- voltage


const int xpin = A3; // x-axis 


const int ypin = A2; // y-axis


const int zpin = A1; // z-axis





int Xoffset;


int Yoffset;


int Zoffset;





int YELLOW = 12;


int GREEN = 11;


int RED = 10;





/*


* These are the activation tresh holds for the LEDs which is calculated from 


* from the current value minus the previous vaule to get the difference 


* e.g. A - B = C the threshold value is C


*/


const int RED_THRESHOLD = 100; 


const int YELLOW_THRESHOLD = 50;


const int GREEN_THRESHOLD = 25;





struct SensorValues


{


int xValue;


int yValue;


int zValue;





SensorValues()


: xValue(0)


, yValue(0)


, zValue(0)


{}





int LengthSqr()


{


//a^2 = b^2 + c^2 + d^2


return (xValue * xValue) + (yValue * yValue) + (zValue * zValue);


}





SensorValues GetDifference( const SensorValues other ) const


{


SensorValues result;


result.xValue = abs(xValue - other.xValue);


result.yValue = abs(yValue - other.yValue);


result.zValue = abs(zValue - other.zValue);





return result;


} 





void Report()


{


Serial.print("X: ");


Serial.print( xValue );


Serial.print("\t"); 





Serial.print("Y: ");


Serial.print( yValue );


Serial.print("\t"); 





Serial.print("Z: ");


Serial.print( zValue );


Serial.print("\t\n"); 


}


};





SensorValues previousReading;





void setup() {


Serial.begin(115200);


pinMode(groundpin, OUTPUT);


pinMode(powerpin, OUTPUT);


digitalWrite(groundpin, LOW);


digitalWrite(powerpin, HIGH);


Xoffset = analogRead(xpin);


Yoffset = analogRead(ypin);


Zoffset = analogRead(zpin);


}





void set_led( int light, int intensity, int activationThreshold )


{


if( intensity > ( activationThreshold * activationThreshold ) )


{


digitalWrite(light,HIGH);


}


else


{


digitalWrite(light,LOW);


}


}





void flash_led(SensorValues & newReading ){





SensorValues difference = newReading.GetDifference(previousReading);


previousReading = newReading; 


difference.Report();





int intensity = difference.LengthSqr();





set_led(RED, intensity, RED_THRESHOLD);


set_led(YELLOW, intensity, YELLOW_THRESHOLD);


set_led(GREEN, intensity, GREEN_THRESHOLD);


}





void loop() {





SensorValues reading;


reading.xValue = analogRead(xpin);


reading.yValue = analogRead(ypin);


reading.zValue = analogRead(zpin);





flash_led(reading);





// delay before next reading:


delay(10);

}
